// Logisim project 4bit_universal_shift.circ as structural Verilog: 1 circuit, main circuit main
module main (
  input  i0,
  input  i1,
  input  i2,
  input  i3,
  input  D,
  input  [1:0] s0s1
);

  wire CLK_out, d_ff_1_q, d_ff_2_q, d_ff_3_q, d_ff_4_q, multiplexer_1_out, multiplexer_2_out,
       multiplexer_3_out, multiplexer_4_out;

  Multiplexer #(.select(2)) multiplexer_1 (
    .in0(D), .in1(d_ff_2_q), .in2(i0), .in3(d_ff_1_q), .out(multiplexer_1_out), .sel(s0s1));
  Clock CLK (.out(CLK_out));
  D_Flip_Flop d_ff_1 (.D(multiplexer_1_out), .clk(CLK_out), .Q(d_ff_1_q));  // open: Qn, preset, reset
  Multiplexer #(.select(2)) multiplexer_2 (
    .in0(d_ff_1_q), .in1(d_ff_3_q), .in2(i1), .in3(d_ff_2_q), .out(multiplexer_2_out), .sel(s0s1));
  LED O0 (.in(d_ff_1_q));
  D_Flip_Flop d_ff_2 (.D(multiplexer_2_out), .clk(CLK_out), .Q(d_ff_2_q));  // open: Qn, preset, reset
  Multiplexer #(.select(2)) multiplexer_3 (
    .in0(d_ff_2_q), .in1(d_ff_4_q), .in2(i2), .in3(d_ff_3_q), .out(multiplexer_3_out), .sel(s0s1));
  D_Flip_Flop d_ff_3 (.D(multiplexer_3_out), .clk(CLK_out), .Q(d_ff_3_q));  // open: Qn, preset, reset
  LED O1 (.in(d_ff_2_q));
  Multiplexer #(.select(2)) multiplexer_4 (
    .in0(d_ff_3_q), .in1(D), .in2(i3), .in3(d_ff_4_q), .out(multiplexer_4_out), .sel(s0s1));
  LED O2 (.in(d_ff_3_q));
  D_Flip_Flop d_ff_4 (.D(multiplexer_4_out), .clk(CLK_out), .Q(d_ff_4_q));  // open: Qn, preset, reset
  LED O3 (.in(d_ff_4_q));

  // Notes on the sheet:
  //   RIGHT->00
  //   LEFT->01
  //   Parallel->10
  //   Retain->11
endmodule
