// Logisim project bcd_adder.circ as structural Verilog: 2 circuits, main circuit main
module main (
  input  in_1,
  input  [3:0] in_2,
  input  [3:0] in_3,
  input  in_4,
  input  in_5,
  input  in_6,
  input  in_7,
  input  in_8,
  input  in_9
);

  wire and_1_out, and_2_out, b_1_cout;
  wire [0:0] or_1_out;
  wire [3:0] b_1_s0, b_2_s0;

  and and_1 (and_1_out, b_1_s0[1], b_1_s0[3]);
  and and_2 (and_2_out, b_1_s0[3], b_1_s0[2]);
  or or_1 (or_1_out[0], b_1_cout, and_1_out, and_2_out);
  b b_1 (
    .Cin(in_1), .A(in_2), .B(in_3), .s0(b_1_s0[0]), .s1(b_1_s0[1]), .s2(b_1_s0[2]), .s3(b_1_s0[3]),
    .Cout(b_1_cout));
  b b_2 (
    .Cin(in_4), .A(b_1_s0), .B({in_6, {2{or_1_out[0]}}, in_5}), .s0(b_2_s0[0]), .s1(b_2_s0[1]),
    .s2(b_2_s0[2]), .s3(b_2_s0[3]));  // open: Cout
  Hex_Digit_Display hex_digit_display_1 (.value({in_9, in_8, in_7, or_1_out[0]}));  // open: dp
  Hex_Digit_Display hex_digit_display_2 (.value(b_2_s0));  // open: dp
endmodule

module b (
  input  Cin,
  input  [3:0] A,
  input  [3:0] B,
  output s0,
  output s1,
  output s2,
  output s3,
  output Cout
);

  wire and_1_out, and_2_out, and_3_out, and_4_out, and_5_out, and_6_out, and_7_out, and_8_out, C1_out,
       C2_out, C3_out, xor_1_out, xor_2_out, xor_4_out, xor_5_out;

  xor xor_1 (xor_1_out, A[0], B[0]);
  and and_1 (and_1_out, A[0], B[0]);
  and and_2 (and_2_out, A[1], B[1]);
  and and_3 (and_3_out, A[2], B[2]);
  xor xor_2 (xor_2_out, A[3], B[3]);
  and and_4 (and_4_out, A[3], B[3]);
  xor xor_3 (s0, Cin, xor_1_out);
  and and_5 (and_5_out, Cin, xor_1_out);
  xor xor_4 (xor_4_out, A[1], B[1]);
  and and_6 (and_6_out, C1_out, xor_4_out);
  xor xor_5 (xor_5_out, A[2], B[2]);
  and and_7 (and_7_out, xor_2_out, C3_out);
  or C1 (C1_out, and_5_out, and_1_out);
  xor xor_6 (s1, C1_out, xor_4_out);
  or C2 (C2_out, and_6_out, and_2_out);
  xor xor_7 (s2, C2_out, xor_5_out);
  and and_8 (and_8_out, C2_out, xor_5_out);
  xor xor_8 (s3, C3_out, xor_2_out);
  or or_1 (Cout, and_7_out, and_4_out);
  or C3 (C3_out, and_8_out, and_3_out);
endmodule
